# Fritzing sketch Arduino1-BlinkLED (saved by Fritzing 0.9.1b)
breadboards: 1

parts:
  Part1 = Arduino Leonardo (Rev3b)
  LED1 = LED - 3mm [color="Red (633nm)" package="3 mm [THT]"]

nets:
  N1: Part1.D9_PWM/A9, LED1.anode
  N2: Part1.GND, LED1.cathode

// code stored in the sketch: Arduino1-BlinkLED.ino
#define LED_PIN 0

void setup () {
  pinMode(LED_PIN, OUTPUT); // Enable pin 13 for digital output
}

void loop () {
  digitalWrite(LED_PIN, HIGH); // Turn on the LED
  delay(1000); // Wait one second (1000 milliseconds)
  digitalWrite(LED_PIN, LOW); // Turn off the LED
  delay(1000); // Wait one second
}
