# Fritzing sketch Arduino2-LEDandPotentiometer (saved by Fritzing 0.9.1b)
circuit board: 8.46667cm x 5.64444cm
breadboards: 1

parts:
  Part1 = Arduino Leonardo (Rev3b)
  LED1 = smd LED [color="Red (633nm)" package="0603 [SMD]"]
  R1 = Rotary Potentiometer (Small) [maximum_resistance=100kΩ package=THT]

nets:
  N1: Part1.5V, R1.leg2
  N2: Part1.A3, R1.wiper
  N3: Part1.D9_PWM/A9, LED1.anode
  N4: Part1.GND, LED1.cathode, R1.leg1

// code stored in the sketch: Arduino2-LEDandPotentiometer.ino
int ledPin = 9;      // LED connected to digital pin 9  
int analogPin = 3;   // potentiometer connected to analog pin 3  
int val = 0;         // variable to store the read value

void setup() {  
  pinMode(ledPin, OUTPUT);   // sets the pin as output  
}

void loop() {  
  val = analogRead(analogPin);   // read the input pin  
  analogWrite(ledPin, val / 4);  // analogRead values go from 0 to 1023, analogWrite values from 0 to 255  
}
