# Fritzing sketch Arduino3-Buttons (saved by Fritzing 0.9.1b)
breadboards: 1

parts:
  Part1 = Arduino Leonardo (Rev3b)
  S1 = Momentary Switch [package=ksa_sealed_tac_switch]
  R1 = Resistor [tolerance=±0.25% resistance=10k package=THT]
  LED1 = LED - 3mm [color="Red (633nm)" package="3 mm [THT]"]

nets:
  N1: Part1.D7, S1.2, R1.Pin_0
  N2: Part1.5V, S1.4
  N3: Part1.D9_PWM/A9, LED1.anode
  N4: Part1.GND, R1.Pin_1, LED1.cathode

// code stored in the sketch: Arduino3-Buttons.ino
const int LED = 9; // the pin for the LED 
const int BUTTON = 7; // the input pin where the // pushbutton is connected 
int val = 0; // val will be used to store the state // of the input pin 
void setup() {
pinMode(LED, OUTPUT); // tell Arduino LED is an output pinMode(BUTTON, INPUT); // and BUTTON is an input 
}
void loop(){ 
val = digitalRead(BUTTON); // read input value and store it 
  // check whether the input is HIGH (button pressed)
 
if (val == HIGH) {
digitalWrite(LED, HIGH); // turn LED ON 
}else{ digitalWrite(LED, LOW); 
} }
