# Fritzing sketch Arduino4-LDR (saved by Fritzing 0.9.1b)
breadboards: 1

parts:
  Part1 = Arduino Leonardo (Rev3b)
  R1 = Resistor [tolerance=±0.25% resistance=10k package=THT]
  LED1 = LED - 3mm [color="Red (633nm)" package="3 mm [THT]"]
  R2 = Photocell (LDR) [package=THT]

nets:
  N1: Part1.5V, R2.pin_0
  N2: Part1.GND, R1.Pin_1, LED1.cathode
  N3: Part1.A0, R1.Pin_0, R2.pin_1
  N4: Part1.D13_PWM, LED1.anode

// code stored in the sketch: Arduino4-LDR.ino
int ledPin = 9;      // LED connected to digital pin 9  
int analogPin = 3;   // LDR connected to analog pin 3  
int val = 0;         // variable to store the read value

void setup() {  
  pinMode(ledPin, OUTPUT);   // sets the pin as output  
}

void loop() {  
  val = analogRead(analogPin);   // read the input pin  
  analogWrite(ledPin, val / 4);  // analogRead values go from 0 to 1023, analogWrite values from 0 to 255  
}
