# Fritzing sketch Arduino5-PdPhysicalInterface (saved by Fritzing 0.9.1b)
breadboards: 1

parts:
  Part1 = Arduino Leonardo (Rev3b)
  R1 = Resistor [tolerance=±0.25% resistance=10k package=THT]
  LED1 = LED - 3mm [color="Red (633nm)" package="3 mm [THT]"]
  R2 = Photocell (LDR) [package=THT]
  R3 = Rotary Potentiometer (Small) [maximum_resistance=100kΩ package=THT]
  S1 = Pushbutton [package="[THT]"]
  R4 = Resistor [tolerance=±0.25% resistance=10k package=THT]
  LED2 = LED - 3mm [color="Green (570nm)" package="3 mm [THT]"]

nets:
  N1: Part1.D7, Part1.5V, R2.pin_0, R3.leg1, S1.Pin_1, S1.Pin_2
  N2: Part1.GND, R1.Pin_1, LED1.cathode, R3.leg2, R4.Pin_0, LED2.cathode
  N3: Part1.A0, R1.Pin_0, R2.pin_1
  N4: Part1.A1, R3.wiper
  N5: Part1.D9_PWM/A9, LED2.anode
  N6: Part1.D10_PWM/A10, LED1.anode
  N7: S1.Pin_3, S1.Pin_4, R4.Pin_1
